# Fritzing sketch Dice (saved by Fritzing 0.9.3b)
circuit board: 8.46667cm x 5.64444cm
perfboards: 3

parts:
  LED2 = LED - 5mm [color="Red (633nm)" package="5 mm [THT]"]
  LED3 = LED - 5mm [color="Red (633nm)" package="5 mm [THT]"]
  LED4 = LED - 5mm [color="Red (633nm)" package="5 mm [THT]"]
  LED5 = LED - 5mm [color="Red (633nm)" package="5 mm [THT]"]
  LED6 = LED - 5mm [color="Red (633nm)" package="5 mm [THT]"]
  LED7 = LED - 5mm [color="Red (633nm)" package="5 mm [THT]"]
  LED8 = LED - 5mm [color="Red (633nm)" package="5 mm [THT]"]
  J3 = male pin header, 5 pins [form="♂ (male)"]  # not connected
  J4 = male pin header, 5 pins [form="♂ (male)"]
  J5 = female pin header, 5 pins [form="♀ (female)"]  # not connected
  J6 = female pin header, 5 pins [form="♀ (female)"]
  R1 = Resistor [tolerance=±5% resistance=220 package=THT]
  R2 = Resistor [tolerance=±5% resistance=220 package=THT]
  R3 = Resistor [tolerance=±5% resistance=220 package=THT]
  R4 = Resistor [tolerance=±5% resistance=220 package=THT]
  U1 = attiny85 [package=dip]
  S1 = Tilt Switch [package=THT]
  Part1 = LilyPad Coin Cell Battery Holder
  J7 = male pin header, 6 pins [form="♂ (male)"]
  J8 = male pin header, 4 pins [form="♂ (male)"]
  J9 = female pin header, 6 pins [form="♀ (female)"]
  J10 = female pin header, 4 pins [form="♀ (female)"]
  R5 = Resistor [tolerance=±5% resistance=220 package=THT]

nets:
  N1: LED2.cathode, LED3.cathode, LED4.cathode, LED5.cathode, LED6.cathode, LED7.cathode, LED8.cathode, J4.pin1
  N2: LED2.anode, LED8.anode, J4.pin4
  N3: LED3.anode, LED7.anode, J4.pin3
  N4: LED4.anode, LED6.anode, J4.pin5
  N5: LED5.anode, J4.pin2
  N6: J6.pin1, R3.Pin_1
  N7: J6.pin2, R2.Pin_1
  N8: J6.pin3, R1.Pin_1
  N9: J6.pin4, R4.Pin_1
  N10: J6.pin5, U1.Pin_4, J8.pin1
  N11: R1.Pin_0, U1.Pin_6
  N12: R2.Pin_0, U1.Pin_5
  N13: R3.Pin_0, U1.Pin_3
  N14: R4.Pin_0, U1.Pin_7
  N15: U1.Pin_2, S1.Pin_2, R5.Pin_1
  N16: U1.Pin_8, S1.Pin_1, J7.pin1
  N17: Part1.-, J10.pin1
  N18: Part1.+, J9.pin1
